# Fritzing sketch Motion Sensor Alarm Sketch (saved by Fritzing 0.9.3b)
circuit board: 8.46667cm x 5.64444cm
breadboards: 1

parts:
  Part1 = Arduino Uno (Rev3)
  LED1 = LED - 5mm [color="Red (633nm)" package="5 mm [THT]"]
  R1 = Resistor [tolerance=±5% resistance=220 package="0805 [SMD]"]
  R2 = Resistor [tolerance=±5% resistance=220 package=THT]
  LED2 = smd LED [color="Green (560nm)" package="0603 [SMD]"]
  R3 = Resistor [tolerance=±5% resistance=220 package=THT]
  Part2 = OLED Monochrome 128x32 I2C [part_number=931]
  PIR1 = PIR sensor
  J1 = Piezo Speaker

nets:
  N1: Part1.A4/SDA, Part2.SDA
  N2: Part1.A5/SCL, Part2.SCL
  N3: Part1.D9_PWM, LED1.cathode
  N4: Part1.D11_PWM/MOSI, LED2.cathode
  N5: Part1.D13/SCK, R2.Pin_1
  N6: Part1.D2, PIR1.SIG
  5V: Part1.5V, PIR1.VDD
  GND: Part1.GND, R1.Pin_1, R3.Pin_1, Part2.GND, PIR1.GND, J1.pin1
  N7: LED1.anode, R1.Pin_0
  N8: R2.Pin_0, J1.pin2
  N9: LED2.anode, R3.Pin_0

custom parts:
  OLED Monochrome 128x32 I2C: These displays are small, only about 1" diagonal, but very readable due to the high contrast of an OLED display. This display is made of 128x32 individual white OLED pixels, each one is turned on or off by the controller chip. Because the display makes its own light, no backlight is required. This reduces the power required to run the OLED and is why the display has such high contrast; we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
